# Fritzing sketch ESP32_My_Mob_Alert_f6 (saved by Fritzing 1.0.6)

parts:
  U1 = ESP32S-HiLetgo [part_number=ESP32S-HiLetgo]
  S3 = Pushbutton [package="[THT]"]
  S4 = Pushbutton [package="[THT]"]
  R1 = Resistor [tolerance=±5% resistance=100 package="0603 [SMD]"]
  M4 = NEO-M8N GPS Module [part_number=GY-GPSV3-NEO]
  M5 = RioRand LM2596
  J2 = Power Jack [package=power_jack_slot]
  LED1 = smd LED [color="Red (633nm)" package="0805 [SMD]"]
  LED2 = smd LED [color="Green (570nm)" package="0805 [SMD]"]
  SG1 = Buzzer 12mm [package=buzzer-ccv]

nets:
  N1: U1.GPIO25, LED1.anode
  N2: U1.GPIO26, LED2.anode
  N3: U1.GPIO27, S3.Pin_3, S3.Pin_4
  GND: U1.GND, S3.Pin_1, S3.Pin_2, S4.Pin_4, R1.Pin_1, M4.GND, M5.Pin_4, SG1.2
  N4: U1.GPIO13, SG1.1
  VIN: U1.VIN, M4.Vcc, M5.Pin_3
  N5: U1.GPIO0, S4.Pin_2
  N6: U1.GPIO18, M4.Rx
  N7: U1.GPIO19, M4.Tx
  N8: R1.Pin_0, LED1.cathode, LED2.cathode
  N9: M5.Pin_1, J2.PWR
  N10: M5.Pin_2, J2.GND

notes:
  GNSS chipset ou par connexion RS232-TTL ou RS422-TTL
  résistance 100 ohm
  témoin alimentation
  position valide
  déclenchement Alerte
  Reset configuration, optionnel, identique bouton boot/iO0
  sinon, GNSS en entrée par UDP
  RS232-TTL ou RS422-TTL, GND, TX, RX, VCC
  sinon, connexion en sortie par UDP
  5.0 volts
  7 à 14 volts
  régulateur LM2596 si alimentation par batterie
  alimentation par USB et/ou connexion en sortie
  buzzer actif, optionnel

custom parts:
  ESP32S-HiLetgo: HiLetgo ESP-WROOM-32 ESP32 ESP-32S Development Board 2.4GHz Dual-Mode WiFi + Bluetooth Dual Cores Microcontroller The ESP32 integrated with Antenna switches, RF Balun, power amplifiers, low-noise amplifiers, filters, and management modules, and the entire solution occupies the least area of PCB. 2.4 GHz Wi-Fi plus Bluetooth dual-mode chip, with TSMC Ultra-low power consumption 40nm technology,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
  NEO-M8N GPS Module: GY-GPSV3-NEO NEO-M8N GPS Module Module based on U-blox NEO-M8N GPS engine, incorporating regulator for 3.3-5V DC input, MS621FE-compatible rechargeable battery for backup and EEPROM for storing configuration settings. Links: NEO-M8 series Product Summary NEO-M8 Datasheet
